// Logisim project rg8.circ as structural Verilog
module demi_add (
  input  a,
  input  b,
  output s,
  output r
);

  xor xor_1 (s, a, b);
  and and_1 (r, a, b);
endmodule
